# Fritzing sketch Receiver (saved by Fritzing 0.9.3b)
circuit board: 12.4cm x 8.8cm
breadboards: 1

parts:
  Teensy_3_2 = Teensy 3.1
  LED_Board_Pin_Input = shrouded pin header, 16 pins [form="♂ (shrouded male)"]
  RF_Module = NRF24L01+ Breakout Board
  LiPo_Battery_-_110mAh = LIPO-2000mAh [package=lipo-2000]
  Switch = SPST Switch [package=ayz0202]
  BLE_Module = Adafruit Bluefruit LE UART Friend [part_number="Adafruit #2479"]
  Voltage_Step-Up = DC-DC CONVERTER [part_number=80633 package=dc-dc_converter]
  LED_Vin = Header 4 [package=screwterminal-3.5mm-4_lock]
  10uF = Capacitor Polarized [package=cpol-radial-10uf-25v]

nets:
  GND: Teensy_3_2.GND, LED_Board_Pin_Input.pin9, LED_Board_Pin_Input.pin13, LED_Board_Pin_Input.pin15, RF_Module.GND, LiPo_Battery_-_110mAh.-, BLE_Module.GND, BLE_Module.CTS, Voltage_Step-Up.IN-, 10uF.-
  N1: Teensy_3_2.D0, RF_Module.CE
  N2: Teensy_3_2.D1, RF_Module.CS
  N3: Teensy_3_2.D2, LED_Board_Pin_Input.pin1
  N4: Teensy_3_2.D3, Teensy_3_2.D8, LED_Board_Pin_Input.pin10
  N5: Teensy_3_2.D4, LED_Board_Pin_Input.pin8
  N6: Teensy_3_2.D5, LED_Board_Pin_Input.pin16
  N7: Teensy_3_2.D6, LED_Board_Pin_Input.pin2
  N8: Teensy_3_2.D7, LED_Board_Pin_Input.pin14
  N9: Teensy_3_2.D9, LED_Board_Pin_Input.pin5
  N10: Teensy_3_2.D10, LED_Board_Pin_Input.pin12
  N11: Teensy_3_2.D11, RF_Module.MOSI
  N12: Teensy_3_2.D12, RF_Module.MISO
  3V3: Teensy_3_2.3V3, RF_Module.VCC, BLE_Module.VIN, 10uF.+
  N13: Teensy_3_2.D13, RF_Module.SCK
  N14: Teensy_3_2.A0/D14, LED_Board_Pin_Input.pin7
  N15: Teensy_3_2.A2/D16, BLE_Module.TXO
  N16: Teensy_3_2.A3/D17, BLE_Module.RXI
  N17: Teensy_3_2.A5/D19, BLE_Module.DFU
  N18: Teensy_3_2.A6/D20, LED_Board_Pin_Input.pin4
  N19: Teensy_3_2.A7/D21, LED_Board_Pin_Input.pin3
  N20: Teensy_3_2.A8/D22, LED_Board_Pin_Input.pin6
  N21: Teensy_3_2.A9/D23, LED_Board_Pin_Input.pin11
  N22: Teensy_3_2.Vin, Switch.P, Voltage_Step-Up.IN+
  N23: LiPo_Battery_-_110mAh.+, Switch.O
  N24: Voltage_Step-Up.OUT-, LED_Vin.3, LED_Vin.4
  N25: Voltage_Step-Up.OUT+, LED_Vin.1, LED_Vin.2

custom parts:
  Adafruit Bluefruit LE UART Friend: The Bluefruit LE UART Friend makes it easy to add Bluetooth Low Energy connectivity to anything with a hardware or software serial port. We even have nice hardware flow control so you won't have to think about losing data. Connect to your Arduino or other microcontroller or even just a standard FTDI cable for debugging and testing.
  DC-DC CONVERTER: WYHP 5A constant current/voltage manufactured by Shenzhen Weiyapuhua Technology Co., Ltd
