# Fritzing sketch Controller4.6 (saved by Fritzing 0.9.3b)
circuit board: 7.2cm x 7.2cm
breadboards: 1

parts:
  U2 = SWITCH_SPDT [package=kps-1290]
  S8 = Pushbutton [package="[THT]"]
  S9 = Pushbutton [package="[THT]"]
  S10 = Pushbutton [package="[THT]"]
  S11 = Pushbutton [package="[THT]"]
  S12 = Pushbutton [package="[THT]"]
  S14 = Pushbutton [package="[THT]"]
  S13 = Pushbutton [package="[THT]"]
  Part3 = 12 NeoPixel Ring [part_number=1643]
  Teensy_3_2 = Teensy 3.1
  Part5 = NRF24L01+ Breakout Board
  C2 = Electrolytic Capacitor [capacitance=10μF package="0605 [SMD, electrolytic]"]
  U3 = LIPO-110mAh [package=lipo-110]

nets:
  N1: U2.P, Teensy_3_2.Vin
  N2: U2.S, U3.+
  N3: S8.Pin_1, S8.Pin_2, Teensy_3_2.A5/D19
  GND: S8.Pin_3, S8.Pin_4, S9.Pin_3, S9.Pin_4, S10.Pin_3, S10.Pin_4, S11.Pin_3, S11.Pin_4, S12.Pin_3, S12.Pin_4, S14.Pin_3, S14.Pin_4, S13.Pin_3, S13.Pin_4, Part3.GND, Teensy_3_2.GND, Part5.GND, C2.-, U3.-
  N4: S9.Pin_1, S9.Pin_2, Teensy_3_2.A4/D18
  N5: S10.Pin_1, S10.Pin_2, Teensy_3_2.A3/D17
  N6: S11.Pin_1, S11.Pin_2, Teensy_3_2.A0/D14
  N7: S12.Pin_1, S12.Pin_2, Teensy_3_2.A1/D15
  N8: S14.Pin_1, S14.Pin_2, Teensy_3_2.D2
  N9: S13.Pin_1, S13.Pin_2, Teensy_3_2.A9/D23
  N10: Part3.IN, Teensy_3_2.A7/D21
  VDD: Part3.VDD, Teensy_3_2.3V3, Part5.VCC, C2.+
  N11: Teensy_3_2.D0, Part5.CE
  N12: Teensy_3_2.D1, Part5.CS
  N13: Teensy_3_2.D11, Part5.MOSI
  N14: Teensy_3_2.D12, Part5.MISO
  N15: Teensy_3_2.D13, Part5.SCK

custom parts:
  12 NeoPixel Ring: 12 ultra bright smart LED NeoPixels are arranged in a circle with 1.5" (37mm) outer diameter. The rings are 'chainable' - connect the output pin of one to the input pin of another. Use only one microcontroller pin to control as many as you can chain together! Each LED is addressable as the driver chip is inside the LED. Each one has ~18mA constant current drive so the color will be very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
