# Fritzing sketch Transmitter (saved by Fritzing 0.9.3b)
circuit board: 7.2cm x 7.2cm
breadboards: 1

parts:
  Switch = SWITCH_SPDT [package=kps-1290]
  Btn2 = Pushbutton [package="[THT]"]
  Btn3 = Pushbutton [package="[THT]"]
  Btn4 = Pushbutton [package="[THT]"]
  Btn5 = Pushbutton [package="[THT]"]
  Btn6 = Pushbutton [package="[THT]"]
  Btn1 = Pushbutton [package="[THT]"]
  Btn7 = Pushbutton [package="[THT]"]
  LED = 12 NeoPixel Ring [part_number=1643]
  Teensy_3_2 = Teensy 3.1
  RF_Module = NRF24L01+ Breakout Board
  Cap = Electrolytic Capacitor [capacitance=10μF package="0605 [SMD, electrolytic]"]
  LiPo_Battery_-_4000mAh = LIPO-110mAh [package=lipo-110]

nets:
  N1: Switch.P, Teensy_3_2.Vin
  N2: Switch.S, LiPo_Battery_-_4000mAh.+
  N3: Btn2.Pin_1, Btn2.Pin_2, Teensy_3_2.A5/D19
  GND: Btn2.Pin_3, Btn2.Pin_4, Btn3.Pin_3, Btn3.Pin_4, Btn4.Pin_3, Btn4.Pin_4, Btn5.Pin_3, Btn5.Pin_4, Btn6.Pin_3, Btn6.Pin_4, Btn1.Pin_3, Btn1.Pin_4, Btn7.Pin_3, Btn7.Pin_4, LED.GND, Teensy_3_2.GND, RF_Module.GND, Cap.-, LiPo_Battery_-_4000mAh.-
  N4: Btn3.Pin_1, Btn3.Pin_2, Teensy_3_2.A4/D18
  N5: Btn4.Pin_1, Btn4.Pin_2, Teensy_3_2.A3/D17
  N6: Btn5.Pin_1, Btn5.Pin_2, Teensy_3_2.A0/D14
  N7: Btn6.Pin_1, Btn6.Pin_2, Teensy_3_2.A1/D15
  N8: Btn1.Pin_1, Btn1.Pin_2, Teensy_3_2.D2
  N9: Btn7.Pin_1, Btn7.Pin_2, Teensy_3_2.A9/D23
  N10: LED.IN, Teensy_3_2.A7/D21
  VDD: LED.VDD, Teensy_3_2.3V3, RF_Module.VCC, Cap.+
  N11: Teensy_3_2.D0, RF_Module.CE
  N12: Teensy_3_2.D1, RF_Module.CS
  N13: Teensy_3_2.D11, RF_Module.MOSI
  N14: Teensy_3_2.D12, RF_Module.MISO
  N15: Teensy_3_2.D13, RF_Module.SCK

custom parts:
  12 NeoPixel Ring: 12 ultra bright smart LED NeoPixels are arranged in a circle with 1.5" (37mm) outer diameter. The rings are 'chainable' - connect the output pin of one to the input pin of another. Use only one microcontroller pin to control as many as you can chain together! Each LED is addressable as the driver chip is inside the LED. Each one has ~18mA constant current drive so the color will be very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
